# Fritzing sketch Deska (saved by Fritzing 0.8.7b)
breadboards: 1

parts:
  7_Segment1 = 7 Segment Display
  7_Segment2 = 7 Segment Display
  7_Segment3 = 7 Segment Display
  7_Segment4 = 7 Segment Display
  Q1 = pnp-Powertransistor [package="TO220 [THT]"]
  Q2 = pnp-Powertransistor [package="TO220 [THT]"]
  Q3 = pnp-Powertransistor [package="TO220 [THT]"]
  Q4 = pnp-Powertransistor [package="TO220 [THT]"]

nets:
  N1: 7_Segment1.common_anode, Q1.collector
  N2: 7_Segment2.common_anode, Q2.collector
  N3: 7_Segment3.common_anode, Q3.collector
  N4: 7_Segment4.common_anode, Q4.collector
  N5: Q1.emitter, Q2.emitter, Q3.emitter, Q4.emitter
